# Fritzing sketch Control 1 (saved by Fritzing 1.0.7)
breadboards: 1

parts:
  power_supply_plug = Power plug
  Q1 = Basic FET N-Channel [package="D2Pak [SMD]"]
  R3 = Resistor [tolerance=±5% resistance=100k power=0.25W package=THT]
  pump = DC Motor [voltage_(max)=6V voltage_(min)=3V]
  Part1 = Arduino Uno (Rev3) - ICSP
  U1 = DIODE-ZENER [package=diode-zener]

nets:
  GND: power_supply_plug.GND, Q1.source, R3.Pin_1, Part1.GND
  N1: power_supply_plug.VCC, pump.pin_2, U1.C
  N2: Q1.Gate, R3.Pin_0, Part1.D5_PWM
  N3: Q1.drain, pump.pin_1, U1.A

custom parts:
  Basic FET N-Channel: A MOSFET N-Channel Transistor
