# Fritzing sketch Control 3 (saved by Fritzing 1.0.7)
breadboards: 1

parts:
  power_supply_plug = Power plug
  Q1 = Basic FET N-Channel [package="D2Pak [SMD]"]
  R3 = Resistor [tolerance=±5% resistance=100k power=0.25W package=THT]
  pump = DC Motor [voltage_(max)=6V voltage_(min)=3V]
  Q3 = Basic FET N-Channel [package="D2Pak [SMD]"]
  R9 = Resistor [tolerance=±5% resistance=100k power=0.25W package=THT]
  solenoid_valve = Solenoid
  Part1 = Arduino Uno (Rev3) - ICSP
  U1 = DIODE-ZENER [package=diode-zener]
  U2 = DIODE-ZENER [package=diode-zener]
  M5Stack_Pressure_Sensor = NCIR [package="SIP (Single Inline) [THT]"]

nets:
  GND: power_supply_plug.GND, Q1.source, R3.Pin_1, Q3.source, R9.Pin_1, Part1.GND, M5Stack_Pressure_Sensor.GND
  N1: power_supply_plug.VCC, pump.pin_2, solenoid_valve.pin2, U1.C, U2.C
  N2: Q1.Gate, R3.Pin_0, Part1.D5_PWM
  N3: Q1.drain, pump.pin_1, U1.A
  N4: Q3.Gate, R9.Pin_0, Part1.D9_PWM
  N5: Q3.drain, solenoid_valve.pin1, U2.A
  N6: Part1.A0, M5Stack_Pressure_Sensor.SCL
  5V: Part1.5V, M5Stack_Pressure_Sensor.VCC

custom parts:
  Basic FET N-Channel: A MOSFET N-Channel Transistor
